# Fritzing sketch patient (saved by Fritzing 1.0.4)
breadboards: 1

parts:
  M1 = MAX30102
  U1 = MLX90614 [package=to-39]
  esp1 = ESP32 DevKitc V4
  Part1 = InvenSense MPU6050
  R1 = Resistor [tolerance=±5% resistance=220 package="0603 [SMD]"]
  R2 = Resistor [tolerance=±5% resistance=220 package="0603 [SMD]"]
  R3 = Resistor [tolerance=±5% resistance=220 package="0603 [SMD]"]
  R4 = Resistor [tolerance=±5% resistance=220 package="0603 [SMD]"]
  LED1 = LED - 3mm [color="Red (633nm)" current=0.030A package="3 mm [THT]"]
  LED2 = LED - 3mm [color="Green (565nm)" current=0.030A package="3 mm [THT]"]
  LED3 = LED - 3mm [color="Red (633nm)" current=0.030A package="3 mm [THT]"]
  LED4 = LED - 3mm [color="Green (565nm)" current=0.030A package="3 mm [THT]"]
  R5 = Resistor [tolerance=±5% resistance=220 package="0603 [SMD]"]
  R6 = Resistor [tolerance=±5% resistance=220 package="0603 [SMD]"]
  LED5 = LED - 3mm [color="Red (633nm)" current=0.030A package="3 mm [THT]"]
  LED6 = LED - 3mm [color="Green (565nm)" current=0.030A package="3 mm [THT]"]
  LED7 = LED - 3mm [color="Red (633nm)" current=0.030A package="3 mm [THT]"]
  LED8 = LED - 3mm [color="Green (565nm)" current=0.030A package="3 mm [THT]"]
  R8 = Resistor [tolerance=±5% resistance=220 package="0603 [SMD]"]
  R9 = Resistor [tolerance=±5% resistance=220 package="0603 [SMD]"]
  R10 = Basic Flex Resistor
  R11 = Resistor [tolerance=±5% resistance=220 package="0603 [SMD]"]

nets:
  VIN: M1.VIN, U1.VDD, esp1.5V, Part1.VCC, R10.pin_1
  N1: M1.SCL, U1.SCL_VZ, esp1.IO22, Part1.SCL
  N2: M1.SDA, U1.PWM_SDA, esp1.IO21, Part1.SDA
  GND: M1.GND, U1.VSS, esp1.GND, Part1.GND, R1.Pin_0, R2.Pin_0, R3.Pin_0, R4.Pin_0, R5.Pin_0, R6.Pin_0, R8.Pin_0, R9.Pin_0, R11.Pin_0
  N3: esp1.IO4, LED1.anode
  N4: esp1.IO16, LED2.anode
  N5: esp1.IO17, LED7.anode
  N6: esp1.IO5, LED4.anode
  N7: esp1.IO18, LED8.anode
  N8: esp1.IO19, LED3.anode
  N9: esp1.IO25, LED6.anode
  N10: esp1.IO26, LED5.anode
  N11: R1.Pin_1, LED1.cathode
  N12: R2.Pin_1, LED2.cathode
  N13: R3.Pin_1, LED3.cathode
  N14: R4.Pin_1, LED4.cathode
  N15: R5.Pin_1, LED5.cathode
  N16: R6.Pin_1, LED6.cathode
  N17: LED7.cathode, R8.Pin_1
  N18: LED8.cathode, R9.Pin_1
  N19: R10.Pin_2, R11.Pin_1

custom parts:
  MAX30102: Oximeter module using the MAX30102 chip. You may wish to read (and check your module) this post on power problems with these modules: https://reedpaper.wordpress.com/2018/08/22/pulse-oximeter-max30100-max30102-how-to-fix-wrong-board/ . As usual, if you want the mounting holes in pcb, you need to drag a hole over the pad in silkscreen to actually drill the hole (by default they are not drilled)
  ESP32 DevKitc V4: ESP32-DevKitC board with ESP32-WROOM-32 module. ESP32-DevKitC V4 is a small-sized ESP32-based development board produced by Espressif. Most of the pins on the ESP module are broken out to the pin headers on the board. The pins D0, D1, D2, D3, CMD and CLK are used internally for communication between ESP32 and SPI flash memory. They are grouped on both sides near the USB connector. Avoid using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
